# Fritzing sketch circuit (saved by Fritzing 0.9.0b)

parts:
  Part1 = Arduino Uno (Rev3)
  LED1 = LED - 5mm [color="Green (555nm)" package="5 mm [THT]"]
  J1 = Piezo Speaker
  R2 = Resistor [tolerance=±5% resistance=560 package=THT]
  R3 = Resistor [tolerance=±5% resistance=1M package=THT]

nets:
  N1: Part1.A0, J1.pin2, R3.Pin_1
  N2: Part1.D13/SCK, R2.Pin_0
  N3: Part1.GND, LED1.cathode, J1.pin1, R3.Pin_0
  N4: LED1.anode, R2.Pin_1

notes:
  Status Light
  Hit Sensor
